// Digital circuit CPU16_Regs.dig as structural Verilog
// Template: register block for a 16-bit CPU (PC/NPC/IR/A/ADDR).
module CPU16_Regs (
  input  ExecEn,
  input  CommitEn,
  input  RESET,
  input  [15:0] IR_in,
  input  [15:0] PC_in,
  input  [15:0] A_in,
  input  [15:0] ADDR_in,
  output [15:0] PC_out,
  output [15:0] NPC_out,
  output [15:0] A_out,
  output [15:0] ADDR_out,
  output [15:0] IR_out
);

  wire undriven_2, undriven_3, undriven_4;
  wire [15:0] undriven;

  D_FF #(.Bits(16)) d_ff_1 (.D(PC_in), .C(CommitEn), .Q(PC_out));  // open: nQ
  D_FF #(.Bits(16)) d_ff_2 (.D(undriven), .C(undriven_2), .Q(NPC_out));  // open: nQ
  D_FF #(.Bits(16)) d_ff_3 (.D(A_in), .C(undriven_3), .Q(A_out));  // open: nQ
  D_FF #(.Bits(16)) d_ff_4 (.D(ADDR_in), .C(undriven_4), .Q(ADDR_out));  // open: nQ
  D_FF #(.Bits(16)) d_ff_5 (.D(IR_in), .C(ExecEn), .Q(IR_out));  // open: nQ
endmodule
