// Digital circuit CPU16_TwoPhase_Template.dig as structural Verilog
// CPU16 Two-Phase Template (Digital)
// This is a *scaffold*: Control16_TwoPhase + CPU16_Regs + InstrMem16 are connected.
// Open the subcircuits (double click the block) and implement your own internals.
// {{de CPU16 Zwei-Phasen-Template (Digital)
// Dies ist ein *Gerüst*: Control16_TwoPhase + CPU16_Regs + InstrMem16 sind verbunden.
// Doppelklick auf die Blöcke, um innen Deine eigene Logik zu implementieren.}}
module CPU16_TwoPhase_Template (
  input  SC,
  input  EN,
  input  RESET,
  output PHASE,
  output ExecEn,
  output CommitEn,
  output [15:0] PC,
  output [15:0] IR,
  output [15:0] ADDR,
  output [15:0] NPC
);

  // Control16_TwoPhase control16_twophase_1: pin names not known; wires that end beside it: RESET, SC, EN
  CPU16_Regs cpu16_regs_1 ();  // open: ExecEn, CommitEn, RESET, IR_in, PC_in, A_in, ADDR_in, PC_out, NPC_out, A_out, ADDR_out, IR_out
  InstrMem16 instrmem16_1 ();  // open: AD, DO

  // Notes on the sheet:
  //   PHASE: Phase indicator
endmodule
