// Logisim project GatedMove.circ as structural Verilog: 3 circuits, main circuit GatedMove
module GatedMove (
  input  I0,
  input  Enable,
  output Q0,
  output Valid
);

  wire and_2_out, nor_1_out, not_1_out, or_1_out;

  not not_1 (not_1_out, Enable);
  and and_1 (Q0, Enable, I0);
  or or_1 (or_1_out, I0, not_1_out);
  and and_2 (and_2_out, or_1_out, Q0);
  nor nor_1 (nor_1_out, Q0, or_1_out);
  or or_2 (Valid, and_2_out, nor_1_out);
endmodule

module TestGatedMove (
  input  I0_in,
  input  En_in,
  output O0,
  output Valid_out
);

  GatedMove TestGatedMove (.I0(I0_in), .Enable(En_in), .Q0(O0), .Valid(Valid_out));
endmodule

module DualRailNAND (
  input  A,
  input  B,
  input  A_En,
  input  B_En,
  output Out0,
  output OutValid
);

  wire and_1_out, nand_1_out;

  nand nand_1 (nand_1_out, A, B);
  and and_1 (and_1_out, A_En, B_En);
  GatedMove gatedmove_1 (.I0(nand_1_out), .Enable(and_1_out), .Q0(Out0), .Valid(OutValid));
endmodule
