// Logisim project SixteenBitProzessor.circ as structural Verilog: 12 circuits, main circuit GatedMove
module EQU (
  input  I0,
  input  I1,
  output O0
);

  wire and_1_out, nor_1_out;

  and and_1 (and_1_out, I1, I0);
  nor nor_1 (nor_1_out, I0, I1);
  or or_1 (O0, and_1_out, nor_1_out);
endmodule

module GatedMove (
  input  Enable,
  input  I0,
  output Valid,
  output Q0
);

  wire not_1_out, or_1_out;

  not not_1 (not_1_out, Enable);
  and and_1 (Q0, Enable, I0);
  EQU Gleich (.I0(Q0), .I1(or_1_out), .O0(Valid));
  or or_1 (or_1_out, I0, not_1_out);
endmodule

module TestGatedMove (
  input  En_in,
  input  I0,
  output En_out,
  output O0
);

  GatedMove TestGatedMove (.Enable(En_in), .I0(I0), .Valid(En_out), .Q0(O0));
endmodule

module DualRailNAND (
  input  A,
  input  B,
  input  A_En,
  input  B_En,
  output Out0,
  output OutValid
);

  wire and_1_out, nand_1_out;

  nand nand_1 (nand_1_out, A, B);
  and and_1 (and_1_out, A_En, B_En);
  GatedMove gatedmove_1 (.Enable(nand_1_out), .I0(and_1_out), .Valid(Out0), .Q0(OutValid));
endmodule

module EightGatedMove (
  input  EnIn,
  input  [7:0] In0To8,
  output EnOut,
  output [7:0] Out0To8
);

  wire gatedmove_1_valid, gatedmove_2_valid, gatedmove_3_valid, gatedmove_4_valid, gatedmove_5_valid,
       gatedmove_6_valid, gatedmove_7_valid, gatedmove_8_valid;

  GatedMove gatedmove_1 (.Enable(EnIn), .I0(In0To8[0]), .Valid(gatedmove_1_valid), .Q0(Out0To8[0]));
  GatedMove gatedmove_2 (.Enable(EnIn), .I0(In0To8[1]), .Valid(gatedmove_2_valid), .Q0(Out0To8[1]));
  GatedMove gatedmove_3 (.Enable(EnIn), .I0(In0To8[2]), .Valid(gatedmove_3_valid), .Q0(Out0To8[2]));
  GatedMove gatedmove_4 (.Enable(EnIn), .I0(In0To8[3]), .Valid(gatedmove_4_valid), .Q0(Out0To8[3]));
  GatedMove gatedmove_5 (.Enable(EnIn), .I0(In0To8[4]), .Valid(gatedmove_5_valid), .Q0(Out0To8[4]));
  GatedMove gatedmove_6 (.Enable(EnIn), .I0(In0To8[5]), .Valid(gatedmove_6_valid), .Q0(Out0To8[5]));
  GatedMove gatedmove_7 (.Enable(EnIn), .I0(In0To8[6]), .Valid(gatedmove_7_valid), .Q0(Out0To8[6]));
  GatedMove gatedmove_8 (.Enable(EnIn), .I0(In0To8[7]), .Valid(gatedmove_8_valid), .Q0(Out0To8[7]));
  and AOut (EnOut, gatedmove_1_valid, gatedmove_2_valid, gatedmove_3_valid, gatedmove_4_valid, gatedmove_5_valid, gatedmove_6_valid, gatedmove_7_valid, gatedmove_8_valid);
endmodule

module SixteenGatedMove (
  input  EnIn,
  input  [15:0] In0To16,
  output EnOut,
  output [15:0] Out0To16
);

  wire eightgatedmove_1_enout, eightgatedmove_2_enout;

  EightGatedMove eightgatedmove_1 (
    .EnIn(EnIn), .In0To8(In0To16[7:0]), .EnOut(eightgatedmove_1_enout), .Out0To8(Out0To16[7:0]));
  EightGatedMove eightgatedmove_2 (
    .EnIn(EnIn), .In0To8(In0To16[15:8]), .EnOut(eightgatedmove_2_enout), .Out0To8(Out0To16[15:8]));
  and AndEn (EnOut, eightgatedmove_1_enout, eightgatedmove_2_enout);
endmodule

module CPU16_Regs (
  input  ExecEn,
  input  CommitEn,
  input  NPC_in0,
  input  NPC_in1,
  input  NPC_in2,
  input  NPC_in3,
  input  NPC_in4,
  input  NPC_in5,
  input  NPC_in6,
  input  NPC_in7,
  input  NPC_in8,
  input  NPC_in9,
  input  NPC_in10,
  input  NPC_in11,
  input  NPC_in12,
  input  NPC_in13,
  input  NPC_in14,
  input  NPC_in15,
  input  A_in0,
  input  A_in1,
  input  A_in2,
  input  A_in3,
  input  A_in4,
  input  A_in5,
  input  A_in6,
  input  A_in7,
  input  ADDR_in0,
  input  ADDR_in1,
  input  ADDR_in2,
  input  ADDR_in3,
  input  ADDR_in4,
  input  ADDR_in5,
  input  ADDR_in6,
  input  ADDR_in7,
  input  ADDR_in8,
  input  ADDR_in9,
  input  ADDR_in10,
  input  ADDR_in11,
  input  ADDR_in12,
  input  ADDR_in13,
  input  ADDR_in14,
  input  ADDR_in15,
  output ExecEnOut,
  output CommitEnOut,
  output NPC0,
  output PC0,
  output NPC1,
  output PC1,
  output NPC2,
  output PC2,
  output NPC3,
  output PC3,
  output NPC4,
  output PC4,
  output NPC5,
  output PC5,
  output NPC6,
  output PC6,
  output NPC7,
  output PC7,
  output NPC8,
  output PC8,
  output NPC9,
  output PC9,
  output NPC10,
  output PC10,
  output NPC11,
  output PC11,
  output NPC12,
  output PC12,
  output NPC13,
  output PC13,
  output NPC14,
  output PC14,
  output NPC15,
  output PC15,
  output A0,
  output A1,
  output A2,
  output A3,
  output A4,
  output A5,
  output A6,
  output A7,
  output ADDR_out0,
  output ADDR_out1,
  output ADDR_out2,
  output ADDR_out3,
  output ADDR_out4,
  output ADDR_out5,
  output ADDR_out6,
  output ADDR_out7,
  output ADDR_out8,
  output ADDR_out9,
  output ADDR_out10,
  output ADDR_out11,
  output ADDR_out12,
  output ADDR_out13,
  output ADDR_out14,
  output ADDR_out15
);

  wire eightgatedmove_1_enout, sixteengatedmove_1_enout, sixteengatedmove_2_enout;

  SixteenGatedMove sixteengatedmove_1 (
    .EnIn(ExecEn),
    .In0To16({NPC_in15, NPC_in14, NPC_in13, NPC_in12, NPC_in11, NPC_in10, NPC_in9, NPC_in8, NPC_in7, NPC_in6, NPC_in5, NPC_in4, NPC_in3, NPC_in2, NPC_in1, NPC_in0}),
    .EnOut(sixteengatedmove_1_enout),
    .Out0To16({PC15, PC14, PC13, PC12, PC11, PC10, PC9, PC8, PC7, PC6, PC5, PC4, PC3, PC2, PC1, PC0}));
  EightGatedMove eightgatedmove_1 (
    .EnIn(ExecEn), .In0To8({A_in7, A_in6, A_in5, A_in4, A_in3, A_in2, A_in1, A_in0}),
    .EnOut(eightgatedmove_1_enout), .Out0To8({A7, A6, A5, A4, A3, A2, A1, A0}));
  SixteenGatedMove sixteengatedmove_2 (
    .EnIn(ExecEn),
    .In0To16({ADDR_in15, ADDR_in14, ADDR_in13, ADDR_in12, ADDR_in11, ADDR_in10, ADDR_in9, ADDR_in8, ADDR_in7, ADDR_in6, ADDR_in5, ADDR_in4, ADDR_in3, ADDR_in2, ADDR_in1, ADDR_in0}),
    .EnOut(sixteengatedmove_2_enout),
    .Out0To16({ADDR_out15, ADDR_out14, ADDR_out13, ADDR_out12, ADDR_out11, ADDR_out10, ADDR_out9, ADDR_out8, ADDR_out7, ADDR_out6, ADDR_out5, ADDR_out4, ADDR_out3, ADDR_out2, ADDR_out1, ADDR_out0}));
  SixteenGatedMove sixteengatedmove_3 (
    .EnIn(CommitEn),
    .In0To16({PC15, PC14, PC13, PC12, PC11, PC10, PC9, PC8, PC7, PC6, PC5, PC4, PC3, PC2, PC1, PC0}),
    .EnOut(CommitEnOut),
    .Out0To16({NPC15, NPC14, NPC13, NPC12, NPC11, NPC10, NPC9, NPC8, NPC7, NPC6, NPC5, NPC4, NPC3, NPC2, NPC1, NPC0}));
  and AndOut (ExecEnOut, sixteengatedmove_1_enout, eightgatedmove_1_enout, sixteengatedmove_2_enout);
endmodule

module PCPlus1Bus16 (
  input  [15:0] PC_in00to16,
  output [15:0] PC_out00to16
);

  Adder #(.width(16)) adder_1 (.a(PC_in00to16), .b(16'h1), .out(PC_out00to16));  // open: cin, cout
endmodule

module EQ2_PC_NPC (
  input  [1:0] PC_in00to01,
  input  [1:0] NPC_in00to01,
  output EqPCNPC
);

  wire equ_1_o0, equ_2_o0;

  EQU equ_1 (.I0(NPC_in00to01[1]), .I1(PC_in00to01[0]), .O0(equ_1_o0));
  EQU equ_2 (.I0(PC_in00to01[1]), .I1(NPC_in00to01[0]), .O0(equ_2_o0));
  and and_1 (EqPCNPC, equ_1_o0, equ_2_o0);
endmodule

module Eq4_PC_NPC (
  input  [3:0] PC_in00to03,
  input  [3:0] NPC_in00to03,
  output EqPCNPC
);

  wire eq2_pc_npc_1_eqpcnpc, eq2_pc_npc_2_eqpcnpc;

  EQ2_PC_NPC eq2_pc_npc_1 (
    .PC_in00to01(NPC_in00to03[3:2]), .NPC_in00to01(PC_in00to03[1:0]), .EqPCNPC(eq2_pc_npc_1_eqpcnpc));
  EQ2_PC_NPC eq2_pc_npc_2 (
    .PC_in00to01(PC_in00to03[3:2]), .NPC_in00to01(NPC_in00to03[1:0]), .EqPCNPC(eq2_pc_npc_2_eqpcnpc));
  and and_1 (EqPCNPC, eq2_pc_npc_1_eqpcnpc, eq2_pc_npc_2_eqpcnpc);
endmodule

module Eq8_PC_NPC (
  input  [7:0] PC_in00to07,
  input  [7:0] NPC_in00to07,
  output EqPCNPC
);

  wire eq4_pc_npc_1_eqpcnpc, eq4_pc_npc_2_eqpcnpc;

  Eq4_PC_NPC eq4_pc_npc_1 (
    .PC_in00to03(NPC_in00to07[7:4]), .NPC_in00to03(PC_in00to07[3:0]), .EqPCNPC(eq4_pc_npc_1_eqpcnpc));
  Eq4_PC_NPC eq4_pc_npc_2 (
    .PC_in00to03(PC_in00to07[7:4]), .NPC_in00to03(NPC_in00to07[3:0]), .EqPCNPC(eq4_pc_npc_2_eqpcnpc));
  and and_1 (EqPCNPC, eq4_pc_npc_1_eqpcnpc, eq4_pc_npc_2_eqpcnpc);
endmodule

module Eq16_PC_NPC2 (
  input  [15:0] PC_in00to16,
  input  [15:0] NPC_in00to16,
  output EqPCNPC
);

  wire and_1_out, and_2_out, and_3_out, and_4_out, and_5_out, and_6_out, and_7_out, and_8_out, and_9_out,
       and_10_out, and_11_out, and_12_out, and_13_out, and_14_out, equ_1_o0, equ_2_o0, equ_3_o0, equ_4_o0,
       equ_5_o0, equ_6_o0, equ_7_o0, equ_8_o0, equ_9_o0, equ_10_o0, equ_11_o0, equ_12_o0, equ_13_o0,
       equ_14_o0, equ_15_o0, equ_16_o0;

  EQU equ_1 (.I0(PC_in00to16[0]), .I1(NPC_in00to16[0]), .O0(equ_1_o0));
  EQU equ_2 (.I0(PC_in00to16[1]), .I1(NPC_in00to16[1]), .O0(equ_2_o0));
  EQU equ_3 (.I0(PC_in00to16[2]), .I1(NPC_in00to16[2]), .O0(equ_3_o0));
  EQU equ_4 (.I0(PC_in00to16[3]), .I1(NPC_in00to16[3]), .O0(equ_4_o0));
  EQU equ_5 (.I0(PC_in00to16[4]), .I1(NPC_in00to16[4]), .O0(equ_5_o0));
  EQU equ_6 (.I0(PC_in00to16[5]), .I1(NPC_in00to16[5]), .O0(equ_6_o0));
  EQU equ_7 (.I0(PC_in00to16[6]), .I1(NPC_in00to16[6]), .O0(equ_7_o0));
  EQU equ_8 (.I0(PC_in00to16[7]), .I1(NPC_in00to16[7]), .O0(equ_8_o0));
  EQU equ_9 (.I0(PC_in00to16[8]), .I1(NPC_in00to16[8]), .O0(equ_9_o0));
  EQU equ_10 (.I0(PC_in00to16[9]), .I1(NPC_in00to16[9]), .O0(equ_10_o0));
  EQU equ_11 (.I0(PC_in00to16[10]), .I1(NPC_in00to16[10]), .O0(equ_11_o0));
  EQU equ_12 (.I0(PC_in00to16[11]), .I1(NPC_in00to16[11]), .O0(equ_12_o0));
  EQU equ_13 (.I0(PC_in00to16[12]), .I1(NPC_in00to16[12]), .O0(equ_13_o0));
  EQU equ_14 (.I0(PC_in00to16[13]), .I1(NPC_in00to16[13]), .O0(equ_14_o0));
  EQU equ_15 (.I0(PC_in00to16[14]), .I1(NPC_in00to16[14]), .O0(equ_15_o0));
  EQU equ_16 (.I0(PC_in00to16[15]), .I1(NPC_in00to16[15]), .O0(equ_16_o0));
  and and_1 (and_1_out, equ_1_o0, equ_2_o0);
  and and_2 (and_2_out, equ_3_o0, equ_4_o0);
  and and_3 (and_3_out, equ_5_o0, equ_6_o0);
  and and_4 (and_4_out, equ_7_o0, equ_8_o0);
  and and_5 (and_5_out, equ_9_o0, equ_10_o0);
  and and_6 (and_6_out, equ_11_o0, equ_12_o0);
  and and_7 (and_7_out, equ_13_o0, equ_14_o0);
  and and_8 (and_8_out, equ_15_o0, equ_16_o0);
  and and_9 (and_9_out, and_1_out, and_2_out);
  and and_10 (and_10_out, and_3_out, and_4_out);
  and and_11 (and_11_out, and_5_out, and_6_out);
  and and_12 (and_12_out, and_7_out, and_8_out);
  and and_13 (and_13_out, and_9_out, and_10_out);
  and and_14 (and_14_out, and_11_out, and_12_out);
  and and_15 (EqPCNPC, and_13_out, and_14_out);
endmodule
